// Logisim project trabalhoSD.circ as structural Verilog
module \controlador_veículos  (
  input  BS,
  input  SP,
  output S0_Verde,
  output S1_Amarelo,
  output S2_Vermelho
);

  wire and_1_out, and_2_out, and_3_out, and_4_out, and_5_out, and_6_out, and_7_out, and_8_out, clock_1_out,
       D0_q, D0_qn, D1_q, D1_qn, D2_qn, or_1_out, or_2_out, or_3_out;

  Clock clock_1 (.out(clock_1_out));
  and and_1 (and_1_out, D1_q, D0_q);
  and and_2 (and_2_out, S2_Vermelho, D0_qn);
  and and_3 (and_3_out, D1_q, D0_qn);
  and and_4 (and_4_out, D2_qn, D1_qn, D0_q);
  and and_5 (and_5_out, SP, S2_Vermelho, D1_qn, D0_qn);
  and and_6 (and_6_out, BS, SP, D0_qn);
  and and_7 (and_7_out, BS, D2_qn, D1_qn, D0_qn);
  D_Flip_Flop D2 (.clk(clock_1_out), .D(or_1_out), .Q(S2_Vermelho), .Qn(D2_qn));  // open: preset, en, reset
  or or_1 (or_1_out, and_1_out, and_2_out);
  D_Flip_Flop D1 (.clk(clock_1_out), .D(or_2_out), .Q(D1_q), .Qn(D1_qn));  // open: preset, en, reset
  or or_2 (or_2_out, and_3_out, and_4_out);
  D_Flip_Flop D0 (.clk(clock_1_out), .D(or_3_out), .Q(D0_q), .Qn(D0_qn));  // open: preset, en, reset
  or or_3 (or_3_out, and_3_out, and_5_out, and_6_out, and_7_out);
  and and_8 (and_8_out, D2_qn, D1_qn, D0_q);
  and and_9 (S0_Verde, D2_qn, D1_qn, D0_qn);
  or or_4 (S1_Amarelo, D1_q, and_8_out);
endmodule

module \controlador_peões  (
  input  SV,
  output S0_Vermelho,
  output S1_Amarelo,
  output S2_Vermelho,
  output Da,
  output Db,
  output Dc,
  output Dd,
  output De,
  output Df,
  output Dg
);

  wire and_1_out, and_2_out, and_3_out, and_4_out, and_5_out, and_6_out, and_7_out, and_8_out, and_9_out,
       and_10_out, and_11_out, and_12_out, and_13_out, and_14_out, and_15_out, and_16_out, and_17_out,
       and_18_out, and_19_out, and_21_out, and_22_out, and_23_out, and_24_out, and_25_out, and_26_out,
       and_27_out, and_28_out, and_29_out, and_30_out, clock_1_out, D0_q, D0_qn, D1_q, D1_qn, D2_q, D2_qn,
       D3_q, D3_qn, or_3_out, or_4_out, or_5_out, or_7_out;

  and and_1 (and_1_out, D0_q, D1_q, D2_qn, D3_qn);
  and and_2 (and_2_out, D3_qn, D2_q, D1_qn);
  and and_3 (and_3_out, D3_qn, D2_q, D0_qn);
  or or_1 (Da, and_1_out, and_2_out, and_3_out, and_4_out);
  and and_4 (and_4_out, D3_q, D2_qn, D1_qn);
  and and_5 (and_5_out, D3_qn, D1_q, D0_q);
  and and_6 (and_6_out, D3_qn, D2_q, D1_qn, D0_qn);
  and and_7 (and_7_out, D3_q, D1_q, D0_qn);
  or or_2 (Db, and_4_out, and_5_out, and_6_out, and_7_out);
  and and_8 (and_8_out, D3_q, D2_qn);
  and and_9 (and_9_out, D3_q, D0_qn);
  and and_10 (and_10_out, D2_q, D1_q, D0_q);
  and and_11 (and_11_out, D3_qn, D2_q, D1_qn);
  and and_12 (and_12_out, D2_q, D0_qn);
  and and_13 (and_13_out, D2_qn, D1_q, D0_q);
  and and_14 (and_14_out, D1_q, D0_qn);
  and and_15 (and_15_out, D3_qn, D1_qn, D0_q);
  and and_16 (and_16_out, D2_qn, D1_qn, D0_q);
  and and_17 (and_17_out, D1_qn, D0_qn, SV);
  Clock clock_1 (.out(clock_1_out));
  or or_3 (or_3_out, and_8_out, and_9_out, and_10_out);
  or or_4 (or_4_out, and_11_out, and_12_out, and_13_out);
  or or_5 (or_5_out, and_14_out, and_15_out, and_16_out);
  and and_18 (and_18_out, D3_q, D2_qn, D0_qn);
  or or_6 (Dc, and_22_out, and_5_out, and_18_out);
  D_Flip_Flop D3 (.clk(clock_1_out), .D(or_3_out), .Q(D3_q), .Qn(D3_qn));  // open: preset, en, reset
  D_Flip_Flop D2 (.clk(clock_1_out), .D(or_4_out), .Q(D2_q), .Qn(D2_qn));  // open: preset, en, reset
  D_Flip_Flop D1 (.clk(clock_1_out), .D(or_5_out), .Q(D1_q), .Qn(D1_qn));  // open: preset, en, reset
  D_Flip_Flop D0 (.clk(clock_1_out), .D(or_7_out), .Q(D0_q), .Qn(D0_qn));  // open: preset, en, reset
  or or_7 (or_7_out, and_12_out, and_14_out, and_9_out, and_17_out);
  and and_19 (and_19_out, D2_q, D1_q, D0_qn);
  or or_8 (Dd, and_4_out, and_1_out, and_19_out, and_21_out);
  and and_20 (S0_Vermelho, D3_qn, D2_qn, D1_qn);
  and and_21 (and_21_out, D3_q, D2_qn, D1_qn, D0_q);
  and and_22 (and_22_out, D3_qn, D2_q);
  and and_23 (and_23_out, D1_q, D0_qn);
  or or_9 (S1_Amarelo, and_22_out, and_23_out, and_24_out, and_25_out);
  and and_24 (and_24_out, D3_q, D2_qn, D1_qn);
  and and_25 (and_25_out, D3_qn, D1_q);
  and and_26 (and_26_out, D3_q, D2_q);
  or or_10 (S2_Vermelho, and_26_out, and_27_out);
  and and_27 (and_27_out, D3_q, D1_q, D0_q);
  or or_11 (De, and_1_out, and_21_out, and_28_out);
  and and_28 (and_28_out, D3_q, D2_q, D1_qn, D0_q);
  and and_29 (and_29_out, D2_q, D1_q);
  or or_12 (Df, and_5_out, and_29_out, and_30_out);
  and and_30 (and_30_out, D3_qn, D2_q, D0_q);
  or or_13 (Dg, and_29_out, and_30_out, and_5_out, and_4_out);
endmodule

module dois_juntos (
  input  \Botão_Sensor 
);

  wire \controlador_peões_1_s0_vermelho , \controlador_veículos_1_s2_vermelho ;

  \controlador_veículos  \controlador_veículos_1  (
    .BS(\Botão_Sensor ), .SP(\controlador_peões_1_s0_vermelho ),
    .S2_Vermelho(\controlador_veículos_1_s2_vermelho ));  // open: S0_Verde, S1_Amarelo
  \controlador_peões  \controlador_peões_1  (
    .SV(\controlador_veículos_1_s2_vermelho ), .S0_Vermelho(\controlador_peões_1_s0_vermelho ));  // open: Da, Db, Dc, Dd, De, Df, Dg, S1_Amarelo, S2_Vermelho
endmodule
